// Logisim project ex4.circ as structural Verilog: 5 circuits, main circuit RotRight
module RotRight (
  input  [15:0] INPUT0,
  input  [3:0] AMOUNT,
  output [15:0] OUTPUT0
);

  wire [15:0] rotate1, rotate2, rotate3, rotate4, rotate5, rotate6, rotate7, rotate8, rotate9, rotate10,
       rotate11, rotate12, rotate13, rotate14, rotate15;

  rot1 rot1_1 (.out_2(rotate3), .in_1(rotate2));
  rot1 rot1_2 (.out_2(rotate5), .in_1(rotate4));
  rot2 rot2_1 (.out_2(rotate6), .in_1(rotate4));
  rot1 rot1_3 (.out_2(rotate7), .in_1(rotate6));
  rot1 rot1_4 (.out_2(rotate9), .in_1(rotate8));
  rot2 rot2_2 (.out_2(rotate10), .in_1(rotate8));
  rot1 rot1_5 (.out_2(rotate11), .in_1(rotate10));
  rot4 rot4_1 (.out_2(rotate12), .in_1(rotate8));
  rot1 rot1_6 (.out_2(rotate13), .in_1(rotate12));
  rot2 rot2_3 (.out_2(rotate14), .in_1(rotate12));
  rot1 rot1_7 (.out_2(rotate15), .in_1(rotate14));
  rot1 rot1_8 (.out_2(rotate1), .in_1(INPUT0));
  rot2 rot2_4 (.out_2(rotate2), .in_1(INPUT0));
  rot4 rot4_2 (.out_2(rotate4), .in_1(INPUT0));
  rot8 rot8_1 (.out_2(rotate8), .in_1(INPUT0));
  Multiplexer #(.enable("false"), .select(4), .width(16)) multiplexer_1 (
    .in0(INPUT0), .in1(rotate1), .in2(rotate2), .in3(rotate3), .in4(rotate4), .in5(rotate5), .in6(rotate6),
    .in7(rotate7), .in8(rotate8), .in9(rotate9), .in10(rotate10), .in11(rotate11), .in12(rotate12),
    .in13(rotate13), .in14(rotate14), .in15(rotate15), .out(OUTPUT0), .sel(AMOUNT));

  // Other names for the same wires on the sheet: amt[3:0] = AMOUNT; origin[15:0] = INPUT0
endmodule

module rot1 (
  input  [15:0] in_1,
  output [15:0] out_2
);

  assign out_2 = {1'b0, in_1[15:1]} | {in_1[0], {15{1'b0}}};  // OR_Gate or_1, 16 bits wide
endmodule

module rot2 (
  input  [15:0] in_1,
  output [15:0] out_2
);

  assign out_2 = {2'b00, in_1[15:2]} | {in_1[1:0], {14{1'b0}}};  // OR_Gate or_1, 16 bits wide
endmodule

module rot4 (
  input  [15:0] in_1,
  output [15:0] out_2
);

  assign out_2 = {4'b0000, in_1[15:4]} | {in_1[3:0], {12{1'b0}}};  // OR_Gate or_1, 16 bits wide
endmodule

module rot8 (
  input  [15:0] in_1,
  output [15:0] out_2
);

  assign out_2 = {{8{1'b0}}, in_1[15:8]} | {in_1[7:0], {8{1'b0}}};  // OR_Gate or_1, 16 bits wide
endmodule
