// Logisim project ex2.circ as structural Verilog: 1 circuit, main circuit compute_BrUn
module compute_BrUn (
  input  [31:0] INSTRUCTION,
  output BrUn
);

  wire [1:1] and_1_out;

  assign {and_1_out[1], BrUn} = INSTRUCTION[14:13] & 2'b11;  // AND_Gate and_1, 2 bits wide
endmodule
